# Fritzing sketch carro_microcontrolado (saved by Fritzing 0.7.7b)
breadboards: 1

parts:
  IC1 = IC, DIP package, 20 pins [chip_label=L293C part_number=L293C]
  Arduino1 = Arduino
  Motor_2_Traseiro = DC Motor
  Motor_1_Dianteiro = DC Motor
  VCC1 = 4 x AAA Battery Mount
  VCC2 = Battery block 9V
  S1 = Pushbutton [package=THT]
  S2 = Pushbutton [package=THT]
  Detector_de_Colisão = Pushbutton [package=THT]
  LED1_Colisão = LED - 5mm [color="Red (633nm)" package="5 mm [THT]"]
  R1 = Resistor [tolerance=±5% resistance=220 package=THT]

nets:
  N1: IC1.pin1, Arduino1.D3
  N2: IC1.pin2, Arduino1.D4
  N3: IC1.pin3, Motor_1_Dianteiro.pin_2
  GND: IC1.pin5, IC1.pin6, IC1.pin15, IC1.pin16, Arduino1.GND, VCC1.-, VCC2.-, S1.leg1, S2.leg1, Detector_de_Colisão.leg1, LED1_Colisão.cathode
  N4: IC1.pin7, Motor_1_Dianteiro.pin_1
  N5: IC1.pin8, Arduino1.D5
  N6: IC1.pin9, IC1.pin20, Arduino1.+5V
  N7: IC1.pin10, VCC1.+
  N8: IC1.pin11, Arduino1.D8
  N9: IC1.pin12, Arduino1.D9
  N10: IC1.pin13, Motor_2_Traseiro.pin_2
  N11: IC1.pin18, Motor_2_Traseiro.pin_1
  N12: IC1.pin19, Arduino1.D10
  N13: Arduino1.D12, Detector_de_Colisão.leg0
  N14: Arduino1.D11, R1.Pin_0
  N15: Arduino1.D7, S1.leg0
  N16: Arduino1.D6, S2.leg0
  N17: Arduino1.VIN, VCC2.+
  N18: LED1_Colisão.anode, R1.Pin_1

notes:
  Arduino Pinagem
  Motor 1 - dianteiro:
  D3 -en1
  D4 - in1
  D5 - in2
  Motor 2 - traseiro:
  D8 - en2
  D9 - in3
  D10 - in4
  Carro com Controle Automatizado
